// Logisim project traffic-light-system.circ as structural Verilog: 12 circuits, main circuit main
module main (
  input  Signal,
  input  Zero,
  input  [2:0] Mode
);

  wire clock_1_out, diff_detector_1_output, G1, G2, G3, G4, GL1, GL2, GL3, GL4, P1, P2, P3, P4, PG1, PG2,
       PG3, PG4, PR1, PR2, PR3, PR4, R1, R2, R3, R4, Y1, Y2, Y3, Y4;
  wire [2:0] E, N, S, W;
  wire [3:0] n4_bit_counter_1_d0;

  Clock clock_1 (.out(clock_1_out));
  traffic_signal traffic_signal_1 (
    .in_1(E), .out_3(R2), .out_4(Y2), .out_6(G2), .out_8(PG2), .out_7(PR2), .in_2(P2), .out_5(GL2));
  _4_bit_counter u_4_bit_counter_1 (
    .Power(Signal), .Zero(Zero), .d0(n4_bit_counter_1_d0[0]), .d1(n4_bit_counter_1_d0[1]),
    .d2(n4_bit_counter_1_d0[2]), .d3(n4_bit_counter_1_d0[3]), .Clock(clock_1_out),
    .in_4(diff_detector_1_output));
  diff_detector diff_detector_1 (.Mode(Mode), .Output(diff_detector_1_output), .Clock(clock_1_out));
  traffic_signal traffic_signal_2 (
    .in_1(N), .out_3(R3), .out_4(Y3), .out_6(G3), .out_8(PG3), .out_7(PR3), .in_2(P3), .out_5(GL3));
  Hex_Digit_Display hex_digit_display_1 (.value(n4_bit_counter_1_d0));  // open: dp
  traffic_signal traffic_signal_3 (
    .in_1(W), .out_3(R4), .out_4(Y4), .out_6(G4), .out_8(PG4), .out_7(PR4), .in_2(P4), .out_5(GL4));
  traffic_signal traffic_signal_4 (
    .in_1(S), .out_3(R1), .out_4(Y1), .out_6(G1), .out_8(PG1), .out_7(PR1), .in_2(P1), .out_5(GL1));
  controller controller_1 (
    .Counter_input(n4_bit_counter_1_d0), .Mode(Mode), .South(S), .East(E), .North(N), .West(W), .PedS(P1),
    .PedE(P2), .PedN(P3), .PedW(P4));
  LED led_1 (.in(R4));
  LED led_2 (.in(Y4));
  LED led_3 (.in(GL4));
  LED led_4 (.in(G4));
  LED led_5 (.in(PR4));
  LED led_6 (.in(PG4));
  LED led_7 (.in(G3));
  LED led_8 (.in(GL3));
  LED led_9 (.in(R3));
  LED led_10 (.in(Y3));
  LED led_11 (.in(PR3));
  LED led_12 (.in(PG3));
  LED led_13 (.in(PR1));
  LED led_14 (.in(PG1));
  LED led_15 (.in(Y1));
  LED led_16 (.in(G1));
  LED led_17 (.in(R1));
  LED led_18 (.in(GL1));
  LED led_19 (.in(PR2));
  LED led_20 (.in(PG2));
  LED led_21 (.in(G2));
  LED led_22 (.in(GL2));
  LED led_23 (.in(Y2));
  LED led_24 (.in(R2));

  // Notes on the sheet:
  //   Clock
  //   NORTH
  //   EAST
  //   Control Circuit
  //   System v2.1.0
  //   Released on Jun 5, 2021
  //   Copyright (c) 2021 Capella87
  //   github.com/Capella87/traffic-light-system
  //   WEST
  //   SOUTH
  //   State
  //   100: Red-flickering
  //   110, 111: Turn-off
  //   WEST
  //   Mode Information
  //   000: Simultaneous
  //   001: Left-turn-after-go-straight
  //   010: Go-straight-after-left-turn
  //   011: Permitted-left-turn
  //   101: Yellow-flickering
  //   Traffic Light System in crossroad
  //   NORTH
  //   SOUTH
  //   EAST
endmodule

module _4_bit_counter (
  input  Power,
  input  Zero,
  input  Clock,
  input  in_4,
  output d0,
  output d1,
  output d2,
  output d3
);

  wire and_1_out, and_2_out, not_1_out, or_1_out;

  or or_1 (or_1_out, Zero, in_4);
  not not_1 (not_1_out, Clock);
  J_K_Flip_Flop j_k_ff_1 (.J(Power), .clk(not_1_out), .K(Power), .Q(d0), .reset(or_1_out));  // open: Qn, preset, en
  and and_1 (and_1_out, d0, d1);
  J_K_Flip_Flop j_k_ff_2 (.J(d0), .clk(not_1_out), .K(d0), .Q(d1), .en(Power), .reset(or_1_out));  // open: Qn, preset
  J_K_Flip_Flop j_k_ff_3 (
    .J(and_1_out), .clk(not_1_out), .K(and_1_out), .Q(d2), .en(Power), .reset(or_1_out));  // open: Qn, preset
  and and_2 (and_2_out, d0, d1, d2);
  J_K_Flip_Flop j_k_ff_4 (
    .J(and_2_out), .clk(not_1_out), .K(and_2_out), .Q(d3), .en(Power), .reset(or_1_out));  // open: Qn, preset

  // Notes on the sheet:
  //   Diff
endmodule

module controller (
  input  [3:0] Counter_input,
  input  [2:0] Mode,
  output [2:0] South,
  output [2:0] East,
  output [2:0] North,
  output [2:0] West,
  output PedS,
  output PedE,
  output PedN,
  output PedW
);

  wire go_straight_after_left_turn_1_pede, go_straight_after_left_turn_1_pedn,
       left_turn_after_go_straight_1_pede, left_turn_after_go_straight_1_pedn, nand_1_out, not_1_out,
       permitted_left_turn_1_pede, permitted_left_turn_1_pedn, simultaneous_1_pede, simultaneous_1_pedn,
       simultaneous_1_peds, simultaneous_1_pedw;
  wire [2:0] go_straight_after_left_turn_1_east, go_straight_after_left_turn_1_south,
       left_turn_after_go_straight_1_east, left_turn_after_go_straight_1_south, permitted_left_turn_1_east,
       permitted_left_turn_1_south, red_flickering_1_east, red_flickering_1_south, simultaneous_1_east,
       simultaneous_1_north, simultaneous_1_south, simultaneous_1_west, yellow_flickering_1_east,
       yellow_flickering_1_south;

  not not_1 (not_1_out, Mode[0]);
  Multiplexer #(.select(3)) multiplexer_1 (
    .in0(simultaneous_1_peds), .in1(left_turn_after_go_straight_1_pedn),
    .in2(go_straight_after_left_turn_1_pedn), .in3(permitted_left_turn_1_pedn), .out(PedS), .sel(Mode),
    .en(not_1_out));  // open: in4, in5, in6, in7
  Multiplexer #(.select(3)) multiplexer_2 (
    .in0(simultaneous_1_pede), .in1(left_turn_after_go_straight_1_pede),
    .in2(go_straight_after_left_turn_1_pede), .in3(permitted_left_turn_1_pede), .out(PedE), .sel(Mode),
    .en(not_1_out));  // open: in4, in5, in6, in7
  simultaneous simultaneous_1 (
    .Counter(Counter_input), .South(simultaneous_1_south), .East(simultaneous_1_east),
    .North(simultaneous_1_north), .West(simultaneous_1_west), .PedS(simultaneous_1_peds),
    .PedW(simultaneous_1_pedw), .PedN(simultaneous_1_pedn), .PedE(simultaneous_1_pede));
  left_turn_after_go_straight left_turn_after_go_straight_1 (
    .Counter(Counter_input), .South(left_turn_after_go_straight_1_south),
    .East(left_turn_after_go_straight_1_east), .PedE(left_turn_after_go_straight_1_pede),
    .PedN(left_turn_after_go_straight_1_pedn));
  go_straight_after_left_turn go_straight_after_left_turn_1 (
    .Counter(Counter_input), .South(go_straight_after_left_turn_1_south),
    .East(go_straight_after_left_turn_1_east), .PedE(go_straight_after_left_turn_1_pede),
    .PedN(go_straight_after_left_turn_1_pedn));
  permitted_left_turn permitted_left_turn_1 (
    .Counter(Counter_input), .South(permitted_left_turn_1_south), .East(permitted_left_turn_1_east),
    .PedE(permitted_left_turn_1_pede), .PedN(permitted_left_turn_1_pedn));
  red_flickering red_flickering_1 (
    .Counter(Counter_input), .South(red_flickering_1_south), .East(red_flickering_1_east));
  yellow_flickering yellow_flickering_1 (
    .Counter(Counter_input), .South(yellow_flickering_1_south), .East(yellow_flickering_1_east));
  Multiplexer #(.select(3)) multiplexer_3 (
    .in0(simultaneous_1_pedn), .in1(left_turn_after_go_straight_1_pedn),
    .in2(go_straight_after_left_turn_1_pedn), .in3(permitted_left_turn_1_pedn), .out(PedN), .sel(Mode),
    .en(not_1_out));  // open: in4, in5, in6, in7
  Multiplexer #(.select(3)) multiplexer_4 (
    .in0(simultaneous_1_pedw), .in1(left_turn_after_go_straight_1_pede),
    .in2(go_straight_after_left_turn_1_pede), .in3(permitted_left_turn_1_pede), .out(PedW), .sel(Mode),
    .en(not_1_out));  // open: in4, in5, in6, in7
  nand nand_1 (nand_1_out, Mode[1], Mode[2]);
  Multiplexer #(.select(3), .width(3)) multiplexer_5 (
    .in0(simultaneous_1_south), .in1(left_turn_after_go_straight_1_south),
    .in2(go_straight_after_left_turn_1_south), .in3(permitted_left_turn_1_south),
    .in4(red_flickering_1_south), .in5(yellow_flickering_1_south), .out(South), .sel(Mode), .en(nand_1_out));  // open: in6, in7
  Multiplexer #(.select(3), .width(3)) multiplexer_6 (
    .in0(simultaneous_1_east), .in1(left_turn_after_go_straight_1_east),
    .in2(go_straight_after_left_turn_1_east), .in3(permitted_left_turn_1_east), .in4(red_flickering_1_east),
    .in5(yellow_flickering_1_east), .out(East), .sel(Mode), .en(nand_1_out));  // open: in6, in7
  Multiplexer #(.select(3), .width(3)) multiplexer_7 (
    .in0(simultaneous_1_north), .in1(left_turn_after_go_straight_1_south),
    .in2(go_straight_after_left_turn_1_south), .in3(permitted_left_turn_1_south),
    .in4(red_flickering_1_south), .in5(yellow_flickering_1_south), .out(North), .sel(Mode), .en(nand_1_out));  // open: in6, in7
  Multiplexer #(.select(3), .width(3)) multiplexer_8 (
    .in0(simultaneous_1_west), .in1(left_turn_after_go_straight_1_east),
    .in2(go_straight_after_left_turn_1_east), .in3(permitted_left_turn_1_east), .in4(red_flickering_1_east),
    .in5(yellow_flickering_1_east), .out(West), .sel(Mode), .en(nand_1_out));  // open: in6, in7

  // Notes on the sheet:
  //   Simultaneous
endmodule

module traffic_signal (
  input  [2:0] in_1,
  input  in_2,
  output out_3,
  output out_4,
  output out_5,
  output out_6,
  output out_7,
  output out_8
);

  wire and_3_out, and_4_out, not_1_out, not_2_out, not_3_out, not_4_out, not_5_out, not_6_out, not_7_out,
       or_1_out, or_2_out, or_4_out;

  not not_1 (not_1_out, in_1[0]);
  not not_2 (not_2_out, in_1[1]);
  not not_3 (not_3_out, in_1[0]);
  not not_4 (not_4_out, in_1[2]);
  not not_5 (not_5_out, in_1[0]);
  not not_6 (not_6_out, in_1[1]);
  not not_7 (not_7_out, in_1[2]);
  not not_8 (out_7, in_2);
  and and_1 (out_3, not_1_out, or_1_out);
  or or_1 (or_1_out, not_2_out, in_1[2]);
  and and_2 (out_4, in_1[1], or_2_out);
  or or_2 (or_2_out, in_1[2], not_3_out);
  and and_3 (and_3_out, in_1[0], in_1[1], not_4_out);
  or or_3 (out_5, and_3_out, and_4_out);
  and and_4 (and_4_out, not_5_out, not_6_out, in_1[2]);
  and and_5 (out_6, in_1[0], or_4_out);
  or or_4 (or_4_out, in_1[1], not_7_out);
  LED led_1 (.in(out_3));
  LED led_2 (.in(out_4));
  LED led_3 (.in(out_5));
  LED led_4 (.in(out_6));
  LED led_5 (.in(out_7));
  LED led_6 (.in(in_2));

  assign out_8 = in_2;

  // Other names for the same wires on the sheet: G = out_6; GL = out_5; PG = in_2; PR = out_7; R = out_3; Y = out_4

  // Notes on the sheet:
  //   Car traffic light
  //   Pedestrian Light
  //   Traffic Light Information
  //   000: Red (Stop)
  //   001: Green (Go straight)
  //   010: Yellow (Change to Red)
  //   101: Turn off all lights
  //   011: Green (Go straight and left turn)
  //   100: Red with left turn green (Left turn only)
  //   110: Red with yellow (Change to Red)
  //   111: Yellow with Green (Change to go straight)
  //   Note: 101 is not used in this system
endmodule

module diff_detector (
  input  [2:0] Mode,
  input  Clock,
  output Output
);

  wire comparator_1_output, comparator_2_output, comparator_3_output, d_ff_1_q, d_ff_2_q, d_ff_3_q;

  D_Flip_Flop d_ff_1 (.clk(Clock), .D(Mode[0]), .Q(d_ff_1_q));  // open: Qn, preset, en, reset
  D_Flip_Flop d_ff_2 (.clk(Clock), .D(Mode[1]), .Q(d_ff_2_q));  // open: Qn, preset, en, reset
  D_Flip_Flop d_ff_3 (.clk(Clock), .D(Mode[2]), .Q(d_ff_3_q));  // open: Qn, preset, en, reset
  comparator comparator_1 (.d1(d_ff_1_q), .d2(Mode[0]), .\output (comparator_1_output));
  comparator comparator_2 (.d1(d_ff_2_q), .d2(Mode[1]), .\output (comparator_2_output));
  comparator comparator_3 (.d1(d_ff_3_q), .d2(Mode[2]), .\output (comparator_3_output));
  nand nand_1 (Output, comparator_1_output, comparator_2_output, comparator_3_output);
endmodule

module comparator (
  input  d1,
  input  d2,
  output \output 
);

  xnor xnor_1 (\output , d1, d2);
endmodule

module simultaneous (
  input  [3:0] Counter,
  output [2:0] South,
  output [2:0] East,
  output [2:0] North,
  output [2:0] West,
  output PedS,
  output PedE,
  output PedN,
  output PedW
);

  wire nand_1_out, not_1_out, not_2_out;

  not not_1 (not_1_out, Counter[3]);
  not not_2 (not_2_out, Counter[2]);
  and and_1 (East[1], Counter[2], not_1_out);
  and and_2 (North[1], not_2_out, Counter[3]);
  and and_3 (West[1], Counter[2], Counter[3]);
  nor nor_1 (South[1], Counter[2], Counter[3]);
  nand nand_1 (nand_1_out, Counter[0], Counter[1]);
  and and_4 (PedE, nand_1_out, South[1]);
  and and_5 (East[0], nand_1_out, East[1]);
  and and_6 (North[0], nand_1_out, North[1]);
  and and_7 (PedS, nand_1_out, West[1]);

  assign East[2] = 1'b0;
  assign North[2] = 1'b0;
  assign PedN = East[0];
  assign PedW = North[0];
  assign {South[2], South[0]} = {1'b0, PedE};
  assign {West[2], West[0]} = {1'b0, PedS};
endmodule

module left_turn_after_go_straight (
  input  [3:0] Counter,
  output [2:0] South,
  output [2:0] East,
  output PedE,
  output PedN
);

  wire and_1_out, and_2_out, and_4_out, and_5_out, and_6_out, nor_1_out, not_1_out, not_2_out, not_3_out,
       not_4_out, or_1_out, or_2_out, or_3_out;

  not not_1 (not_1_out, Counter[2]);
  not not_2 (not_2_out, Counter[0]);
  not not_3 (not_3_out, Counter[1]);
  and and_1 (and_1_out, Counter[1], Counter[0]);
  nor nor_1 (nor_1_out, Counter[1], Counter[0]);
  nor nor_2 (PedE, Counter[2], Counter[3]);
  and and_2 (and_2_out, Counter[2], not_4_out);
  not not_4 (not_4_out, Counter[3]);
  or or_1 (or_1_out, Counter[0], Counter[1]);
  and and_3 (East[0], not_1_out, Counter[3]);
  and and_4 (and_4_out, Counter[3], Counter[2]);
  and and_5 (and_5_out, Counter[0], Counter[1]);
  or or_2 (or_2_out, and_5_out, and_6_out);
  and and_6 (and_6_out, not_2_out, not_3_out);
  or or_3 (or_3_out, and_1_out, nor_1_out);
  and and_7 (South[1], or_3_out, and_2_out);
  and and_8 (South[2], and_2_out, or_1_out);
  and and_9 (East[2], or_1_out, and_4_out);
  and and_10 (East[1], and_4_out, or_2_out);

  assign PedN = East[0];
  assign South[0] = PedE;

  // Other names for the same wires on the sheet: Ped2 = East[0]; Ped1 = PedE

  // Notes on the sheet:
  //   PedS
  //   PedW
  //   North
  //   West
endmodule

module go_straight_after_left_turn (
  input  [3:0] Counter,
  output [2:0] South,
  output [2:0] East,
  output PedE,
  output PedN
);

  wire and_1_out, and_2_out, and_3_out, and_4_out, and_5_out, and_6_out, and_7_out, and_8_out, and_11_out,
       and_12_out, and_15_out, and_16_out, nor_1_out, nor_2_out, nor_3_out, not_1_out, not_2_out, not_3_out,
       not_4_out, or_1_out, or_2_out;

  not not_1 (not_1_out, Counter[2]);
  nor nor_1 (nor_1_out, Counter[2], Counter[0]);
  and and_1 (and_1_out, Counter[2], Counter[0]);
  not not_2 (not_2_out, Counter[3]);
  and and_2 (and_2_out, not_2_out, Counter[1]);
  and and_3 (and_3_out, Counter[0], Counter[1]);
  nor nor_2 (nor_2_out, Counter[2], Counter[3]);
  not not_3 (not_3_out, Counter[3]);
  and and_4 (and_4_out, not_3_out, Counter[2]);
  and and_5 (and_5_out, not_1_out, Counter[3]);
  nor nor_3 (nor_3_out, Counter[0], Counter[2]);
  and and_6 (and_6_out, Counter[0], Counter[2]);
  and and_7 (and_7_out, Counter[1], Counter[3]);
  and and_8 (and_8_out, Counter[2], Counter[3]);
  or or_1 (or_1_out, nor_1_out, and_1_out);
  and and_9 (South[1], or_1_out, and_2_out);
  not not_4 (not_4_out, and_3_out);
  and and_10 (South[2], not_4_out, nor_2_out);
  and and_11 (and_11_out, and_3_out, nor_2_out);
  and and_12 (and_12_out, not_4_out, and_4_out);
  and and_13 (East[2], not_4_out, and_5_out);
  or or_2 (or_2_out, nor_3_out, and_6_out);
  or or_3 (PedE, and_11_out, and_12_out);
  and and_14 (East[1], or_2_out, and_7_out);
  and and_15 (and_15_out, and_5_out, and_3_out);
  and and_16 (and_16_out, not_4_out, and_8_out);
  or or_4 (East[0], and_15_out, and_16_out);

  assign PedN = East[0];
  assign South[0] = PedE;

  // Other names for the same wires on the sheet: Ped2 = East[0]; Ped1 = PedE

  // Notes on the sheet:
  //   PedS
  //   PedW
  //   North
  //   West
endmodule

module permitted_left_turn (
  input  [3:0] Counter,
  output [2:0] South,
  output [2:0] East,
  output PedE,
  output PedN
);

  wire and_2_out, not_1_out, not_2_out, not_3_out, not_4_out, or_1_out;

  not not_1 (not_1_out, Counter[3]);
  not not_2 (not_2_out, Counter[0]);
  not not_3 (not_3_out, Counter[1]);
  not not_4 (not_4_out, Counter[2]);
  and and_1 (PedE, not_1_out, or_1_out);
  and and_2 (and_2_out, Counter[0], Counter[1], Counter[2]);
  or or_1 (or_1_out, not_2_out, not_3_out, not_4_out);
  and and_3 (East[0], or_1_out, Counter[3]);
  and and_4 (South[1], not_1_out, and_2_out);
  and and_5 (East[1], and_2_out, Counter[3]);

  assign East[2] = 1'b0;
  assign PedN = East[0];
  assign {South[2], South[0]} = {1'b0, PedE};

  // Other names for the same wires on the sheet: Ped2 = East[0]; Ped1 = PedE

  // Notes on the sheet:
  //   PedS
  //   PedW
  //   North
  //   West
endmodule

module red_flickering (
  input  [3:0] Counter,
  output [2:0] South,
  output [2:0] East
);

  not not_1 (East[2], Counter[0]);

  assign East[1:0] = {1'b0, East[2]};
  assign South = {Counter[0], 1'b0, Counter[0]};

  // Notes on the sheet:
  //   North
  //   West
endmodule

module yellow_flickering (
  input  [3:0] Counter,
  output [2:0] South,
  output [2:0] East
);

  not not_1 (East[1], Counter[0]);
  nand nand_1 (South[2], 1'b1, Counter[0]);
  not not_2 (East[2], South[2]);

  assign East[0] = East[2];
  assign South[1:0] = {Counter[0], South[2]};

  // Notes on the sheet:
  //   North
  //   West
endmodule
